# Fritzing sketch WeatherLogger (saved by Fritzing 0.9.2b)
breadboards: 1

parts:
  Breakout1 = BMP280 [package=Breakout]
  Raspberry_Pi1 = Raspberry Pi B+
  LED1 = LEDs [package=led10mm]
  R1 = Resistor [tolerance=±5% resistance=220 package="0805 [SMD]"]
  LCM1602_IIC1 = LCM1602 IIC [part_number="LCM1602 IIC" chip_label="LCM1602 IIC" package="DIP (Dual Inline) [THT]"]
  SENSOR1 = TCS34725 RGB Color Sensor
  LCD1 = LCD screen

nets:
  VIN: Breakout1.VIN, Raspberry_Pi1.5V, LCM1602_IIC1.VCC, SENSOR1.3V3
  GND: Breakout1.GND, Raspberry_Pi1.GND, LCM1602_IIC1.GND, SENSOR1.LED
  N1: Breakout1.SCK, LCM1602_IIC1.SCL, SENSOR1.SCL
  N2: Breakout1.SDI, Raspberry_Pi1.GPIO2, LCM1602_IIC1.SDA, SENSOR1.SDA
  N3: Raspberry_Pi1.3V3, R1.Pin_1
  N4: Raspberry_Pi1.GIPO12, LED1.A
  N5: LED1.C, R1.Pin_0
  VSS: LCM1602_IIC1.VSS, LCD1.VSS
  VDD: LCM1602_IIC1.VDD, LCD1.VDD
  N6: LCM1602_IIC1.V0, LCD1.V0
  N7: LCM1602_IIC1.RS, LCD1.RS
  N8: LCM1602_IIC1.RW, LCD1.R/W
  N9: LCM1602_IIC1.E, LCD1.E
  N10: LCM1602_IIC1.D0, LCD1.DB0
  N11: LCM1602_IIC1.D1, LCD1.DB1
  N12: LCM1602_IIC1.D2, LCD1.DB2
  N13: LCM1602_IIC1.D3, LCD1.DB3
  N14: LCM1602_IIC1.D4, LCD1.DB4
  N15: LCM1602_IIC1.D5, LCD1.DB5
  N16: LCM1602_IIC1.D6, LCD1.DB6
  N17: LCM1602_IIC1.D7, LCD1.DB7
  N18: LCM1602_IIC1.A, LCD1.LED+
  N19: LCM1602_IIC1.K, LCD1.LED-
  N20: LCM1602_IIC1.LED_A, LCM1602_IIC1.LED_B

custom parts:
  BMP280: Barometric Pressure and Temperature Sensor
  Raspberry Pi B+: The awesome Raspberry Pi ARM Board with 40 pin gipo. Ready for special designed Raspberry Pi B+ Hat (Hardware attached (on) top)
  LCM1602 IIC: I2C-Module to use a 1602 or 2004 LCD on with the wire.h libory Serial LCD Modul
  TCS34725 RGB Color Sensor: TCS34725 RGB Color Sensor with LED
